// Logisim project Sap1 Logisim Simulation.circ as structural Verilog: 13 circuits, main circuit AC
module AC (
  input  Ea,
  input  CLK,
  input  CLR,
  input  [7:0] bus_input,
  input  nLa,
  output [7:0] adder_sub_output,
  output [7:0] bus_output
);

  wire not_1_out;
  wire [7:0] controlled_buffer_1_out;

  D_Flip_Flop D7 (.clk(CLK), .D(controlled_buffer_1_out[7]), .Q(CLR), .reset(CLR));  // open: Qn, preset, en
  assign controlled_buffer_1_out = not_1_out ? bus_input : 8'bz;  // Controlled_Buffer controlled_buffer_1
  not not_1 (not_1_out, nLa);
  D_Flip_Flop d_ff_1 (
    .clk(CLK), .D(controlled_buffer_1_out[6]), .Q(adder_sub_output[6]), .preset(CLR), .en(CLR), .reset(CLR));  // open: Qn
  D_Flip_Flop d_ff_2 (
    .clk(CLK), .D(controlled_buffer_1_out[5]), .Q(adder_sub_output[5]), .reset(CLR));  // open: Qn, preset, en
  D_Flip_Flop d_ff_3 (
    .clk(CLK), .D(controlled_buffer_1_out[4]), .Q(adder_sub_output[4]), .reset(CLR));  // open: Qn, preset, en
  assign bus_output = Ea ? {CLR, adder_sub_output[6:0]} : 8'bz;  // Controlled_Buffer controlled_buffer_2
  D_Flip_Flop d_ff_4 (
    .clk(CLK), .D(controlled_buffer_1_out[3]), .Q(adder_sub_output[3]), .reset(CLR));  // open: Qn, preset, en
  D_Flip_Flop d_ff_5 (
    .clk(CLK), .D(controlled_buffer_1_out[2]), .Q(adder_sub_output[2]), .reset(CLR));  // open: Qn, preset, en
  D_Flip_Flop d_ff_6 (
    .clk(CLK), .D(controlled_buffer_1_out[1]), .Q(adder_sub_output[1]), .reset(CLR));  // open: Qn, preset, en
  D_Flip_Flop D0 (
    .clk(CLK), .D(controlled_buffer_1_out[0]), .Q(adder_sub_output[0]), .reset(CLR));  // open: Qn, preset, en

  assign adder_sub_output[7] = CLR;
endmodule

module B (
  input  CLK,
  input  clr,
  input  [7:0] bus_inpuyttt,
  input  nLb,
  output [7:0] adder__sub_output
);

  wire not_1_out;
  wire [7:0] controlled_buffer_1_out;

  D_Flip_Flop D7 (
    .clk(CLK), .D(controlled_buffer_1_out[7]), .Q(adder__sub_output[7]), .en(clr), .reset(clr));  // open: Qn, preset
  D_Flip_Flop d_ff_1 (
    .clk(CLK), .D(controlled_buffer_1_out[6]), .Q(adder__sub_output[6]), .reset(clr));  // open: Qn, preset, en
  D_Flip_Flop d_ff_2 (
    .clk(CLK), .D(controlled_buffer_1_out[5]), .Q(adder__sub_output[5]), .reset(clr));  // open: Qn, preset, en
  D_Flip_Flop d_ff_3 (
    .clk(CLK), .D(controlled_buffer_1_out[4]), .Q(adder__sub_output[4]), .reset(clr));  // open: Qn, preset, en
  not not_1 (not_1_out, nLb);
  D_Flip_Flop d_ff_4 (
    .clk(CLK), .D(controlled_buffer_1_out[3]), .Q(adder__sub_output[3]), .reset(clr));  // open: Qn, preset, en
  D_Flip_Flop d_ff_5 (
    .clk(CLK), .D(controlled_buffer_1_out[2]), .Q(adder__sub_output[2]), .reset(clr));  // open: Qn, preset, en
  assign controlled_buffer_1_out = not_1_out ? bus_inpuyttt : 8'bz;  // Controlled_Buffer controlled_buffer_1
  D_Flip_Flop d_ff_6 (
    .clk(CLK), .D(controlled_buffer_1_out[1]), .Q(adder__sub_output[1]), .reset(clr));  // open: Qn, preset, en
  D_Flip_Flop D0 (
    .clk(CLK), .D(controlled_buffer_1_out[0]), .Q(adder__sub_output[0]), .reset(clr));  // open: Qn, preset, en
endmodule

module output_reg (
  input  CLK,
  input  in_2,
  input  [7:0] bus_input,
  input  nLo,
  output [7:0] display_outputt
);

  wire not_1_out;
  wire [7:0] controlled_buffer_1_out;

  D_Flip_Flop D7 (
    .clk(CLK), .D(controlled_buffer_1_out[7]), .Q(display_outputt[7]), .reset(in_2));  // open: Qn, preset, en
  D_Flip_Flop d_ff_1 (
    .clk(CLK), .D(controlled_buffer_1_out[6]), .Q(display_outputt[6]), .reset(in_2));  // open: Qn, preset, en
  assign controlled_buffer_1_out = not_1_out ? bus_input : 8'bz;  // Controlled_Buffer controlled_buffer_1
  not not_1 (not_1_out, nLo);
  D_Flip_Flop d_ff_2 (
    .clk(CLK), .D(controlled_buffer_1_out[5]), .Q(display_outputt[5]), .reset(in_2));  // open: Qn, preset, en
  D_Flip_Flop d_ff_3 (
    .clk(CLK), .D(controlled_buffer_1_out[4]), .Q(display_outputt[4]), .reset(in_2));  // open: Qn, preset, en
  D_Flip_Flop d_ff_4 (
    .clk(CLK), .D(controlled_buffer_1_out[3]), .Q(display_outputt[3]), .reset(in_2));  // open: Qn, preset, en
  D_Flip_Flop d_ff_5 (
    .clk(CLK), .D(controlled_buffer_1_out[2]), .Q(display_outputt[2]), .reset(in_2));  // open: Qn, preset, en
  D_Flip_Flop d_ff_6 (
    .clk(CLK), .D(controlled_buffer_1_out[1]), .Q(display_outputt[1]), .reset(in_2));  // open: Qn, preset, en
  D_Flip_Flop D0 (
    .clk(CLK), .D(controlled_buffer_1_out[0]), .Q(display_outputt[0]), .reset(in_2));  // open: Qn, preset, en
endmodule

module program_counter (
  input  c_p,
  input  nCLK,
  input  nCLR,
  input  Ep,
  output [3:0] Bus_output
);

  wire j_k_ff_1_q, j_k_ff_2_q, j_k_ff_3_q, j_k_ff_4_q, not_1_out, not_2_out;

  not not_1 (not_1_out, nCLK);
  not not_2 (not_2_out, nCLR);
  J_K_Flip_Flop #(.trigger("falling")) j_k_ff_1 (
    .J(c_p), .clk(not_1_out), .K(c_p), .Q(j_k_ff_1_q), .reset(not_2_out));  // open: Qn, preset, en
  assign Bus_output[0] = Ep ? j_k_ff_1_q : 1'bz;  // Controlled_Buffer controlled_buffer_1
  assign Bus_output[1] = Ep ? j_k_ff_2_q : 1'bz;  // Controlled_Buffer controlled_buffer_2
  J_K_Flip_Flop #(.trigger("falling")) j_k_ff_2 (
    .J(c_p), .clk(j_k_ff_1_q), .K(c_p), .Q(j_k_ff_2_q), .reset(not_2_out));  // open: Qn, preset, en
  assign Bus_output[2] = Ep ? j_k_ff_3_q : 1'bz;  // Controlled_Buffer controlled_buffer_3
  J_K_Flip_Flop #(.trigger("falling")) j_k_ff_3 (
    .J(c_p), .clk(j_k_ff_2_q), .K(c_p), .Q(j_k_ff_3_q), .reset(not_2_out));  // open: Qn, preset, en
  assign Bus_output[3] = Ep ? j_k_ff_4_q : 1'bz;  // Controlled_Buffer controlled_buffer_4
  J_K_Flip_Flop j_k_ff_4 (
    .J(c_p), .clk(j_k_ff_3_q), .K(c_p), .Q(j_k_ff_4_q), .reset(not_2_out));  // open: Qn, preset, en
endmodule

module all (
  input  [3:0] Address,
  input  RUN,
  input  [7:0] Data,
  output [3:0] out_4,
  output [3:0] out_5
);

  wire and_1_out, and_2_out, Clear_RAM_out, CLK_out, controlled_buffer_1_out, not_1_out, not_2_out,
       not_3_out, not_4_out, not_5_out, RESET_out, undriven, undriven_2, undriven_3, undriven_4, undriven_5,
       undriven_6, undriven_7, undriven_8, undriven_9, undriven_10, undriven_11, undriven_12, undriven_13,
       Write_to_RAM_out;
  wire [3:0] IR_to_controller, MAR_to_ram, multiplexer_1_out, O_display_outputt, O_display_outputt_2;
  wire [7:0] AC_adder_sub_output, B_adder__sub_output, PC_bus_output;

  Button Write_to_RAM (.out(Write_to_RAM_out));
  Button Clear_RAM (.out(Clear_RAM_out));
  Multiplexer #(.width(4)) multiplexer_1 (
    .in0(Address), .in1(MAR_to_ram), .out(multiplexer_1_out), .sel(RUN));  // open: en
  not not_1 (not_1_out, RUN);
  Control_Unit Control_Unit (
    .CLK(controlled_buffer_1_out), .I3(IR_to_controller[3]), .I2(IR_to_controller[2]),
    .I1(IR_to_controller[1]), .I0(IR_to_controller[0]), .HLT(undriven_10), .cp(undriven_3), .EP(undriven_4),
    .nLM(undriven_2), .nCE(undriven_5), .nLI(undriven_6), .nLa(undriven_7), .Ea(undriven_12),
    .Su(undriven_13), .Eu(undriven_8), .nLB(undriven_9), .nLo(undriven_11), .nEI(undriven));  // open: CLR
  program_counter PC (
    .c_p(undriven_3), .nCLK(controlled_buffer_1_out), .Ep(undriven_4), .nCLR(RESET_out),
    .Bus_output(PC_bus_output[3:0]));
  MAR MAR (
    .to_ram(MAR_to_ram), .clk(controlled_buffer_1_out), .from_bus(PC_bus_output[3:0]), .nlm(undriven_2));  // open: clr
  and and_1 (and_1_out, not_2_out, Write_to_RAM_out);
  not not_2 (not_2_out, RUN);
  not not_3 (not_3_out, undriven_5);
  not not_4 (not_4_out, RUN);
  ir IR (
    .to_controller(IR_to_controller), .clk(controlled_buffer_1_out), .clr(RESET_out),
    .from_bus(PC_bus_output), .to_bus(PC_bus_output[3:0]), .nLi(undriven_6), .nEi(undriven));
  RAM #(.addrWidth(4), .bus("separate")) ram_1 (
    .addr(multiplexer_1_out), .din(Data), .data(PC_bus_output), .str(not_1_out), .clk(and_1_out),
    .ld(not_3_out), .clr(and_2_out));  // open: sel
  and and_2 (and_2_out, not_4_out, Clear_RAM_out);
  not not_5 (not_5_out, undriven_10);
  Button RESET (.out(RESET_out));
  Clock CLK (.out(CLK_out));
  assign controlled_buffer_1_out = not_5_out ? CLK_out : 1'bz;  // Controlled_Buffer controlled_buffer_1
  Hex_Digit_Display hex_digit_display_1 (.value(O_display_outputt_2));  // open: dp
  AC AC (
    .adder_sub_output(AC_adder_sub_output), .CLK(controlled_buffer_1_out), .bus_input(PC_bus_output),
    .bus_output(PC_bus_output), .nLa(undriven_7), .Ea(undriven_12));  // open: CLR
  ALU ALU (
    .from_B_register(B_adder__sub_output), .To_Bus(PC_bus_output), .SU(undriven_13),
    .from_Accumulator(AC_adder_sub_output), .Eu(undriven_8));
  B B (
    .CLK(controlled_buffer_1_out), .bus_inpuyttt(PC_bus_output), .adder__sub_output(B_adder__sub_output),
    .nLb(undriven_9));  // open: clr
  output_reg O (
    .CLK(controlled_buffer_1_out), .in_2(RESET_out), .bus_input(PC_bus_output),
    .display_outputt({O_display_outputt_2, O_display_outputt}), .nLo(undriven_11));
  Hex_Digit_Display hex_digit_display_2 (.value(O_display_outputt));  // open: dp
endmodule

module ALU (
  input  [7:0] from_B_register,
  input  SU,
  input  Eu,
  input  [7:0] To_Bus,
  input  [7:0] from_Accumulator
);

  wire adder_2_cout, adder_3_cout, adder_4_cout, adder_5_cout, adder_6_cout, adder_7_cout, adder_8_cout,
       xor_1_out, xor_2_out, xor_3_out, xor_4_out, xor_5_out, xor_6_out, xor_7_out, xor_8_out;
  wire [7:0] adder_8_out;

  assign To_Bus = Eu ? adder_8_out : 8'bz;  // Controlled_Buffer controlled_buffer_1
  xor xor_1 (xor_1_out, SU, from_B_register[7]);
  Adder #(.width(1)) adder_1 (
    .a(xor_1_out), .b(from_Accumulator[7]), .out(adder_8_out[7]), .cin(adder_2_cout));  // open: cout
  xor xor_2 (xor_2_out, SU, from_B_register[6]);
  Adder #(.width(1)) adder_2 (
    .a(xor_2_out), .b(from_Accumulator[6]), .out(adder_8_out[6]), .cin(adder_3_cout), .cout(adder_2_cout));
  xor xor_3 (xor_3_out, SU, from_B_register[5]);
  Adder #(.width(1)) adder_3 (
    .a(xor_3_out), .b(from_Accumulator[5]), .out(adder_8_out[5]), .cin(adder_4_cout), .cout(adder_3_cout));
  xor xor_4 (xor_4_out, SU, from_B_register[4]);
  Adder #(.width(1)) adder_4 (
    .a(xor_4_out), .b(from_Accumulator[4]), .out(adder_8_out[4]), .cin(adder_5_cout), .cout(adder_4_cout));
  Adder #(.width(1)) adder_5 (
    .a(xor_5_out), .b(from_Accumulator[3]), .out(adder_8_out[3]), .cin(adder_6_cout), .cout(adder_5_cout));
  xor xor_5 (xor_5_out, SU, from_B_register[3]);
  Adder #(.width(1)) adder_6 (
    .a(xor_6_out), .b(from_Accumulator[2]), .out(adder_8_out[2]), .cin(adder_7_cout), .cout(adder_6_cout));
  xor xor_6 (xor_6_out, SU, from_B_register[2]);
  xor xor_7 (xor_7_out, SU, from_B_register[1]);
  Adder #(.width(1)) adder_7 (
    .a(xor_7_out), .b(from_Accumulator[1]), .out(adder_8_out[1]), .cin(adder_8_cout), .cout(adder_7_cout));
  xor xor_8 (xor_8_out, SU, from_B_register[0]);
  Adder #(.width(1)) adder_8 (
    .a(xor_8_out), .b(from_Accumulator[0]), .out(adder_8_out[0]), .cin(SU), .cout(adder_8_cout));
endmodule

module Control_Unit (
  input  CLK,
  input  CLR,
  input  I3,
  input  I2,
  input  I1,
  input  I0,
  input  HLT,
  input  cp,
  input  EP,
  input  nLM,
  input  nCE,
  input  nLI,
  input  nLa,
  input  Ea,
  input  Su,
  input  Eu,
  input  nLB,
  input  nEI,
  input  nLo
);

  wire and_1_out, and_2_out, and_3_out, and_4_out, and_5_out, and_6_out, and_7_out, and_8_out, and_9_out,
       and_10_out, and_11_out, and_12_out, and_15_out, and_16_out, and_17_out, and_18_out, undriven,
       undriven_2, undriven_3, undriven_4, undriven_5, undriven_6, undriven_7;

  Decoder Instruction_Decoder (
    .I3(I3), .I2(I2), .I1(I1), .I0(I0), .LDA(undriven_4), .ADD(undriven_2), .SUB(undriven), .OUT(undriven_5),
    .HLT(HLT));
  and and_1 (and_1_out, undriven_7, undriven_4);
  and and_2 (and_2_out, undriven_7, undriven_2);
  or or_1 (nLM, EP, and_1_out, and_2_out, and_3_out);
  Ring_Counter Ring_Counter (
    .CLK(CLK), .CLR(CLR), .T1(EP), .T6(undriven_3), .T5(undriven_6), .T4(undriven_7), .T3(nLI), .T2(cp));
  and and_3 (and_3_out, undriven_7, undriven);
  or or_2 (nCE, nLI, and_5_out, and_4_out, and_6_out);
  and and_4 (and_4_out, undriven_6, undriven_2);
  and and_5 (and_5_out, undriven_6, undriven_4);
  and and_6 (and_6_out, undriven_6, undriven);
  and and_7 (and_7_out, undriven_7, undriven_4);
  and and_8 (and_8_out, undriven_7, undriven_2);
  or or_3 (nEI, and_7_out, and_8_out, and_9_out);
  and and_9 (and_9_out, undriven_7, undriven);
  and and_10 (and_10_out, undriven_6, undriven_4);
  and and_11 (and_11_out, undriven_3, undriven_2);
  or or_4 (nLa, and_10_out, and_11_out, and_12_out);
  and and_12 (and_12_out, undriven_3, undriven);
  and and_13 (Su, undriven, undriven_3);
  and and_14 (Ea, undriven_5, undriven_7);
  and and_15 (and_15_out, undriven_2, undriven_3);
  and and_16 (and_16_out, undriven, undriven_3);
  or or_5 (Eu, and_15_out, and_16_out);
  and and_17 (and_17_out, undriven_2, undriven_6);
  or or_6 (nLB, and_17_out, and_18_out);
  and and_18 (and_18_out, undriven, undriven_6);
  and and_19 (nLo, undriven_5, undriven_7);
endmodule

module Ring_Counter (
  input  CLK,
  input  CLR,
  input  T1,
  input  T6,
  input  T5,
  input  T4,
  input  T3,
  input  T2
);

  wire j_k_ff_1_q, j_k_ff_1_qn, j_k_ff_2_q, j_k_ff_2_qn, j_k_ff_3_q, j_k_ff_3_qn, j_k_ff_4_q, j_k_ff_4_qn,
       j_k_ff_5_q, j_k_ff_5_qn, j_k_ff_6_q, j_k_ff_6_qn;

  J_K_Flip_Flop j_k_ff_1 (
    .J(j_k_ff_2_q), .clk(CLK), .K(j_k_ff_2_qn), .Q(j_k_ff_1_q), .Qn(j_k_ff_1_qn), .reset(CLR));  // open: preset, en
  J_K_Flip_Flop j_k_ff_2 (
    .J(j_k_ff_3_q), .clk(CLK), .K(j_k_ff_3_qn), .Q(j_k_ff_2_q), .Qn(j_k_ff_2_qn), .reset(CLR));  // open: preset, en
  J_K_Flip_Flop j_k_ff_3 (
    .J(j_k_ff_4_q), .clk(CLK), .K(j_k_ff_4_qn), .Q(j_k_ff_3_q), .Qn(j_k_ff_3_qn), .reset(CLR));  // open: preset, en
  J_K_Flip_Flop j_k_ff_4 (
    .J(j_k_ff_5_q), .clk(CLK), .K(j_k_ff_5_qn), .Q(j_k_ff_4_q), .Qn(j_k_ff_4_qn), .reset(CLR));  // open: preset, en
  J_K_Flip_Flop j_k_ff_5 (
    .J(j_k_ff_6_qn), .clk(CLK), .K(j_k_ff_6_q), .Q(j_k_ff_5_q), .Qn(j_k_ff_5_qn), .reset(CLR));  // open: preset, en
  J_K_Flip_Flop j_k_ff_6 (
    .J(j_k_ff_1_qn), .clk(CLK), .K(j_k_ff_1_q), .Q(j_k_ff_6_q), .Qn(j_k_ff_6_qn), .reset(CLR));  // open: preset, en
endmodule

module Decoder (
  input  I3,
  input  I2,
  input  I1,
  input  I0,
  input  LDA,
  input  ADD,
  input  SUB,
  input  OUT,
  input  HLT
);

  wire and_1_out, and_2_out, and_3_out, and_4_out, and_5_out, not_1_out, not_2_out, not_3_out, not_4_out;

  not not_1 (not_1_out, I3);
  not not_2 (not_2_out, I2);
  not not_3 (not_3_out, I1);
  not not_4 (not_4_out, I0);
  and and_1 (and_1_out, not_4_out, not_3_out, not_2_out, not_1_out);
  and and_2 (and_2_out, I0, not_3_out, not_2_out, not_1_out);
  and and_3 (and_3_out, not_4_out, I1, not_2_out, not_1_out);
  and and_4 (and_4_out, not_4_out, I1, I2, I3);
  and and_5 (and_5_out, I0, I1, I2, I3);
endmodule

module ir (
  input  nEi,
  input  clk,
  input  clr,
  input  [7:0] from_bus,
  input  nLi,
  output [3:0] to_bus,
  output [3:0] to_controller
);

  wire not_1_out, not_2_out;
  wire [3:0] D0_q;
  wire [7:0] controlled_buffer_1_out;

  D_Flip_Flop D7 (
    .clk(clk), .D(controlled_buffer_1_out[7]), .Q(to_controller[3]), .reset(clr));  // open: Qn, preset, en
  D_Flip_Flop d_ff_1 (
    .clk(clk), .D(controlled_buffer_1_out[6]), .Q(to_controller[2]), .reset(clr));  // open: Qn, preset, en
  D_Flip_Flop d_ff_2 (
    .clk(clk), .D(controlled_buffer_1_out[5]), .Q(to_controller[1]), .reset(clr));  // open: Qn, preset, en
  assign controlled_buffer_1_out = not_1_out ? from_bus : 8'bz;  // Controlled_Buffer controlled_buffer_1
  not not_1 (not_1_out, nLi);
  D_Flip_Flop d_ff_3 (
    .clk(clk), .D(controlled_buffer_1_out[4]), .Q(to_controller[0]), .reset(clr));  // open: Qn, preset, en
  assign to_bus = not_2_out ? D0_q : 4'bz;  // Controlled_Buffer controlled_buffer_2
  not not_2 (not_2_out, nEi);
  D_Flip_Flop d_ff_4 (.clk(clk), .D(controlled_buffer_1_out[3]), .Q(D0_q[3]), .reset(clr));  // open: Qn, preset, en
  D_Flip_Flop d_ff_5 (.clk(clk), .D(controlled_buffer_1_out[2]), .Q(D0_q[2]), .reset(clr));  // open: Qn, preset, en
  D_Flip_Flop d_ff_6 (.clk(clk), .D(controlled_buffer_1_out[1]), .Q(D0_q[1]), .reset(clr));  // open: Qn, preset, en
  D_Flip_Flop D0 (.clk(clk), .D(controlled_buffer_1_out[0]), .Q(D0_q[0]), .reset(clr));  // open: Qn, preset, en
endmodule

module Ram (
  input  Cp,
  input  nclk,
  input  Ep,
  input  clr,
  output [3:0] output_to_bus
);

  wire ha_1_sum, ha_2_carry, ha_2_sum, ha_3_carry, ha_3_sum, ha_4_carry, ha_4_sum, not_1_out;
  wire [3:0] d_ff_4_q;

  not not_1 (not_1_out, nclk);
  HA ha_1 (.A(ha_2_carry), .sum(ha_1_sum), .B(d_ff_4_q[3]));  // open: carry
  HA ha_2 (.A(ha_3_carry), .sum(ha_2_sum), .B(d_ff_4_q[2]), .carry(ha_2_carry));
  D_Flip_Flop d_ff_1 (.clk(not_1_out), .D(ha_1_sum), .Q(d_ff_4_q[3]), .reset(clr));  // open: Qn, preset, en
  HA ha_3 (.A(ha_4_carry), .sum(ha_3_sum), .B(d_ff_4_q[1]), .carry(ha_3_carry));
  D_Flip_Flop d_ff_2 (.clk(not_1_out), .D(ha_2_sum), .Q(d_ff_4_q[2]), .reset(clr));  // open: Qn, preset, en
  HA ha_4 (.A(Cp), .sum(ha_4_sum), .B(d_ff_4_q[0]), .carry(ha_4_carry));
  D_Flip_Flop d_ff_3 (.clk(not_1_out), .D(ha_3_sum), .Q(d_ff_4_q[1]), .reset(clr));  // open: Qn, preset, en
  D_Flip_Flop d_ff_4 (.clk(not_1_out), .D(ha_4_sum), .Q(d_ff_4_q[0]), .reset(clr));  // open: Qn, preset, en
  assign output_to_bus = Ep ? d_ff_4_q : 4'bz;  // Controlled_Buffer controlled_buffer_1
endmodule

module HA (
  input  A,
  input  B,
  output sum,
  output carry
);

  wire and_1_out, xor_1_out;

  xor xor_1 (xor_1_out, A, B);
  // AND_Gate and_1 has open pins: out=and_1_out
endmodule

module MAR (
  input  nlm,
  input  clk,
  input  clr,
  input  [3:0] from_bus,
  output [3:0] to_ram
);

  wire not_1_out;
  wire [3:0] controlled_buffer_1_out;

  not not_1 (not_1_out, nlm);
  assign controlled_buffer_1_out = not_1_out ? from_bus : 4'bz;  // Controlled_Buffer controlled_buffer_1
  D_Flip_Flop d_ff_1 (.clk(clk), .D(controlled_buffer_1_out[3]), .Q(to_ram[3]), .reset(clr));  // open: Qn, preset, en
  D_Flip_Flop d_ff_2 (.clk(clk), .D(controlled_buffer_1_out[2]), .Q(to_ram[2]));  // open: Qn, preset, en, reset
  D_Flip_Flop d_ff_3 (.clk(clk), .D(controlled_buffer_1_out[1]), .Q(to_ram[1]));  // open: Qn, preset, en, reset
  D_Flip_Flop d_ff_4 (.clk(clk), .D(controlled_buffer_1_out[0]), .Q(to_ram[0]));  // open: Qn, preset, en, reset
endmodule
